# Fritzing sketch luminosity_sensor_calibration (saved by Fritzing 1.0.1rc)
breadboards: 1

parts:
  A2 = Arduino Nano ESP32
  R5 = Resistor [tolerance=±5% resistance=10k package="0402 [SMD]"]
  R6 = PHOTOCELL [package=photocell]

nets:
  N1: A2.Pin_2, R6.P$2
  N2: A2.Pin_6, R5.Pin_1, R6.P$1
  N3: A2.Pin_14, A2.Pin_19

notes:
  Board powered by USB

custom parts:
  Arduino Nano ESP32: Arduino® Nano ESP32 smd.
