# Fritzing sketch moist_sensor_calibration (saved by Fritzing 1.0.1rc)
breadboards: 1

parts:
  A2 = Arduino Nano ESP32
  Chirp!_Soil_Moisture_Sensor1 = Chirp! Soil Moisture Sensor v2.7.3

nets:
  N1: A2.Pin_4, Chirp!_Soil_Moisture_Sensor1.pin_3
  N2: A2.Pin_12, Chirp!_Soil_Moisture_Sensor1.Pin_1
  N3: A2.Pin_14, A2.Pin_19, Chirp!_Soil_Moisture_Sensor1.pin_5

notes:
  The actual sensor does not communicate via SPI but returns an analogic value. Consider the "SDA/MOSI" pin as this analog output.

custom parts:
  Arduino Nano ESP32: Arduino® Nano ESP32 smd.
