# Fritzing sketch oled_screen (saved by Fritzing 1.0.1rc)
breadboards: 1

parts:
  A2 = Arduino Nano ESP32
  Grove1 = Grove OLED 128x96

nets:
  N1: A2.Pin_8, Grove1.SDA
  N2: A2.Pin_9, Grove1.SCL
  N3: A2.Pin_12, Grove1.VCC
  N4: A2.Pin_14, A2.Pin_19, Grove1.GND

notes:
  OLED Screen
  powered by USB
  The board is

custom parts:
  Arduino Nano ESP32: Arduino® Nano ESP32 smd.
