# Fritzing sketch test_command_relay_with_push_button (saved by Fritzing 1.0.1rc)
breadboards: 1

parts:
  A1 = Arduino Nano ESP32
  S1 = Momentary Switch [package=ksa_sealed_tac_switch]
  KY-1 = Keyes Relay [package=THT]
  R1 = Resistor [tolerance=±5% resistance=10k package="0402 [SMD]"]
  U2 = Voltage Regulator - 5V [package="TO220 [THT]"]
  M1 = DC Motor [voltage_(max)=6V voltage_(min)=3V]
  VCC1 = Battery block 9V

nets:
  N1: A1.Pin_12, S1.4, KY-1.power
  N2: A1.Pin_14, A1.Pin_19, KY-1.ground, R1.Pin_1, U2.GND, VCC1.-
  N3: A1.Pin_20, S1.1, R1.Pin_0
  N4: A1.Pin_25, KY-1.signal
  N5: KY-1.C, M1.pin_1
  N6: KY-1.NO, U2.output_voltage, M1.pin_2
  N7: U2.input_voltage, VCC1.+

notes:
  VIN / GND / VOUT
  IN / VCC / GND

custom parts:
  Arduino Nano ESP32: Arduino® Nano ESP32 smd.
  Keyes Relay: The Keyes 5V relay module is suitable for SCM development, home appliance control. It uses a 5V~12V TIL control signal which can control DC / AC signal.
