# Fritzing sketch water_level (saved by Fritzing 1.0.1rc)
breadboards: 1

parts:
  A4 = Arduino Nano ESP32
  S4 = Momentary Switch [package=ksa_sealed_tac_switch]
  KY-4 = Keyes Relay [package=THT]
  R11 = Resistor [tolerance=±5% resistance=10k package="0402 [SMD]"]
  VCC4 = Battery block 9V
  U5 = Voltage Regulator - 5V [package="DPak [SMD]"]
  M4 = DC Motor [voltage_(max)=6V voltage_(min)=3V]
  HC-SR04_Sensor_4 = HC-SR04 Ultrasonic Distance Sensor

nets:
  N1: A4.Pin_2, S4.2, HC-SR04_Sensor_4.VCC
  GND: A4.Pin_14, A4.Pin_19, KY-4.ground, KY-4.NO, R11.Pin_0, VCC4.-, U5.GND, HC-SR04_Sensor_4.GND
  N2: A4.Pin_22, S4.3, R11.Pin_1
  N3: A4.Pin_24, HC-SR04_Sensor_4.TRIG
  N4: A4.Pin_26, HC-SR04_Sensor_4.ECHO
  N5: A4.Pin_30, KY-4.signal
  N6: KY-4.power, U5.output_voltage, M4.pin_2
  N7: KY-4.C, M4.pin_1
  N8: VCC4.+, U5.input_voltage

notes:
  Water pump
  IN / 5V / GND
  VIN / GND / VOUT
  The Arduino board is
  powered by USB

custom parts:
  Arduino Nano ESP32: Arduino® Nano ESP32 smd.
  Keyes Relay: The Keyes 5V relay module is suitable for SCM development, home appliance control. It uses a 5V~12V TIL control signal which can control DC / AC signal.
