# Fritzing sketch test_read_potentiometer (saved by Fritzing 1.0.1rc)
breadboards: 1

parts:
  A1 = Arduino Nano ESP32
  R1 = 6mm Trimmer Potentiometer [maximum_resistance=10kΩ knob_status=50% power=0.5W package=THT]

nets:
  N1: A1.Pin_11, R1.wiper
  N2: A1.Pin_14, A1.Pin_19, R1.leg1, R1.leg2

custom parts:
  Arduino Nano ESP32: Arduino® Nano ESP32 smd.
