# Fritzing sketch test_sleep_mode_with_interrupt (saved by Fritzing 1.0.1rc)
breadboards: 1

parts:
  A2 = Arduino Nano ESP32
  S2 = Momentary Switch [package=ksa_sealed_tac_switch]
  R5 = Resistor [tolerance=±5% resistance=220 package="0402 [SMD]"]
  LED3 = smd LED [color="Green (555nm)" package="0603 [SMD]"]
  S3 = Momentary Switch [package=ksa_sealed_tac_switch]
  R6 = Resistor [tolerance=±5% power=0.25W resistance=10k package=THT]

nets:
  N1: A2.Pin_12, S2.4, S3.4
  N2: A2.Pin_14, A2.Pin_19, R5.Pin_1, R6.Pin_0
  N3: A2.Pin_22, S2.1, R6.Pin_1
  N4: A2.Pin_24, S3.1
  N5: A2.Pin_26, LED3.anode
  N6: R5.Pin_0, LED3.cathode

custom parts:
  Arduino Nano ESP32: Arduino® Nano ESP32 smd.
